// Digital circuit register-file.dig as structural Verilog
module register_file (
  input  [4:0] ReadReg1,
  input  [4:0] ReadReg2,
  input  [4:0] WriteReg,
  input  [31:0] WriteData,
  input  RegWrite,
  input  Clock,
  output [31:0] ReadData1,
  output [31:0] ReadData2
);

  wire dec0, dec1, dec2, dec3, dec4, dec5, dec6, dec7, dec8, dec9, dec10, dec11, dec12, dec13, dec14, dec15,
       dec16, dec17, dec18, dec19, dec20, dec21, dec22, dec23, dec24, dec25, dec26, dec27, dec28, dec29,
       dec30, dec31, writeenable0, writeenable1, writeenable2, writeenable3, writeenable4, writeenable5,
       writeenable6, writeenable7, writeenable8, writeenable9, writeenable10, writeenable11, writeenable12,
       writeenable13, writeenable14, writeenable15, writeenable16, writeenable17, writeenable18,
       writeenable19, writeenable20, writeenable21, writeenable22, writeenable23, writeenable24,
       writeenable25, writeenable26, writeenable27, writeenable28, writeenable29, writeenable30,
       writeenable31;
  wire [31:0] R0_out, R1_out, R2_out, R3_out, R4_out, R5_out, R6_out, R7_out, R8_out, R9_out, R10_out,
       R11_out, R12_out, R13_out, R14_out, R15_out, R16_out, R17_out, R18_out, R19_out, R20_out, R21_out,
       R22_out, R23_out, R24_out, R25_out, R26_out, R27_out, R28_out, R29_out, R30_out, R31_out;

  Register #(.Bits(32)) Register_0 (.D({32{1'b0}}), .C(Clock), .en(1'b0), .Q(R0_out));
  Register #(.Bits(32)) Register_8 (.D(WriteData), .C(Clock), .en(writeenable8), .Q(R8_out));
  Register #(.Bits(32)) Register_16 (.D(WriteData), .C(Clock), .en(writeenable16), .Q(R16_out));
  Register #(.Bits(32)) Register_24 (.D(WriteData), .C(Clock), .en(writeenable24), .Q(R24_out));
  Register #(.Bits(32)) Register_1 (.D(WriteData), .C(Clock), .en(writeenable1), .Q(R1_out));
  Register #(.Bits(32)) Register_9 (.D(WriteData), .C(Clock), .en(writeenable9), .Q(R9_out));
  Register #(.Bits(32)) Register_17 (.D(WriteData), .C(Clock), .en(writeenable17), .Q(R17_out));
  Register #(.Bits(32)) Register_25 (.D(WriteData), .C(Clock), .en(writeenable25), .Q(R25_out));
  Register #(.Bits(32)) Register_2 (.D(WriteData), .C(Clock), .en(writeenable2), .Q(R2_out));
  Register #(.Bits(32)) Register_10 (.D(WriteData), .C(Clock), .en(writeenable10), .Q(R10_out));
  Register #(.Bits(32)) Register_18 (.D(WriteData), .C(Clock), .en(writeenable18), .Q(R18_out));
  Register #(.Bits(32)) Register_26 (.D(WriteData), .C(Clock), .en(writeenable26), .Q(R26_out));
  and and_1 (writeenable0, RegWrite, dec0);
  and and_2 (writeenable1, RegWrite, dec1);
  and and_3 (writeenable2, RegWrite, dec2);
  and and_4 (writeenable3, RegWrite, dec3);
  and and_5 (writeenable4, RegWrite, dec4);
  and and_6 (writeenable5, RegWrite, dec5);
  and and_7 (writeenable6, RegWrite, dec6);
  and and_8 (writeenable7, RegWrite, dec7);
  and and_9 (writeenable8, RegWrite, dec8);
  and and_10 (writeenable9, RegWrite, dec9);
  Register #(.Bits(32)) Register_3 (.D(WriteData), .C(Clock), .en(writeenable3), .Q(R3_out));
  Register #(.Bits(32)) Register_11 (.D(WriteData), .C(Clock), .en(writeenable11), .Q(R11_out));
  Register #(.Bits(32)) Register_19 (.D(WriteData), .C(Clock), .en(writeenable19), .Q(R19_out));
  Register #(.Bits(32)) Register_27 (.D(WriteData), .C(Clock), .en(writeenable27), .Q(R27_out));
  Register #(.Bits(32)) Register_4 (.D(WriteData), .C(Clock), .en(writeenable4), .Q(R4_out));
  Register #(.Bits(32)) Register_12 (.D(WriteData), .C(Clock), .en(writeenable12), .Q(R12_out));
  Register #(.Bits(32)) Register_20 (.D(WriteData), .C(Clock), .en(writeenable20), .Q(R20_out));
  Register #(.Bits(32)) Register_28 (.D(WriteData), .C(Clock), .en(writeenable28), .Q(R28_out));
  and and_11 (writeenable10, RegWrite, dec10);
  and and_12 (writeenable11, RegWrite, dec11);
  and and_13 (writeenable12, RegWrite, dec12);
  and and_14 (writeenable13, RegWrite, dec13);
  and and_15 (writeenable14, RegWrite, dec14);
  and and_16 (writeenable15, RegWrite, dec15);
  and and_17 (writeenable16, RegWrite, dec16);
  and and_18 (writeenable17, RegWrite, dec17);
  and and_19 (writeenable18, RegWrite, dec18);
  Register #(.Bits(32)) Register_5 (.D(WriteData), .C(Clock), .en(writeenable5), .Q(R5_out));
  Register #(.Bits(32)) Register_13 (.D(WriteData), .C(Clock), .en(writeenable13), .Q(R13_out));
  Register #(.Bits(32)) Register_21 (.D(WriteData), .C(Clock), .en(writeenable21), .Q(R21_out));
  Register #(.Bits(32)) Register_29 (.D(WriteData), .C(Clock), .en(writeenable29), .Q(R29_out));
  Register #(.Bits(32)) Register_6 (.D(WriteData), .C(Clock), .en(writeenable6), .Q(R6_out));
  Register #(.Bits(32)) Register_14 (.D(WriteData), .C(Clock), .en(writeenable14), .Q(R14_out));
  Register #(.Bits(32)) Register_22 (.D(WriteData), .C(Clock), .en(writeenable22), .Q(R22_out));
  Register #(.Bits(32)) Register_30 (.D(WriteData), .C(Clock), .en(writeenable30), .Q(R30_out));
  Register #(.Bits(32)) Register_7 (.D(WriteData), .C(Clock), .en(writeenable7), .Q(R7_out));
  Register #(.Bits(32)) Register_15 (.D(WriteData), .C(Clock), .en(writeenable15), .Q(R15_out));
  Register #(.Bits(32)) Register_23 (.D(WriteData), .C(Clock), .en(writeenable23), .Q(R23_out));
  Register #(.Bits(32)) Register_31 (.D(WriteData), .C(Clock), .en(writeenable31), .Q(R31_out));
  and and_20 (writeenable19, RegWrite, dec19);
  and and_21 (writeenable20, RegWrite, dec20);
  and and_22 (writeenable21, RegWrite, dec21);
  and and_23 (writeenable22, RegWrite, dec22);
  and and_24 (writeenable23, RegWrite, dec23);
  and and_25 (writeenable24, RegWrite, dec24);
  and and_26 (writeenable25, RegWrite, dec25);
  and and_27 (writeenable26, RegWrite, dec26);
  and and_28 (writeenable27, RegWrite, dec27);
  and and_29 (writeenable28, RegWrite, dec28);
  and and_30 (writeenable29, RegWrite, dec29);
  and and_31 (writeenable30, RegWrite, dec30);
  and and_32 (writeenable31, RegWrite, dec31);
  Decoder #(.Selector_Bits(5)) decoder_1 (
    .sel(WriteReg), .out_0(dec0), .out_1(dec1), .out_2(dec2), .out_3(dec3), .out_4(dec4), .out_5(dec5),
    .out_6(dec6), .out_7(dec7), .out_8(dec8), .out_9(dec9), .out_10(dec10), .out_11(dec11), .out_12(dec12),
    .out_13(dec13), .out_14(dec14), .out_15(dec15), .out_16(dec16), .out_17(dec17), .out_18(dec18),
    .out_19(dec19), .out_20(dec20), .out_21(dec21), .out_22(dec22), .out_23(dec23), .out_24(dec24),
    .out_25(dec25), .out_26(dec26), .out_27(dec27), .out_28(dec28), .out_29(dec29), .out_30(dec30),
    .out_31(dec31));
  Multiplexer #(.Selector_Bits(5), .Bits(32)) multiplexer_1 (
    .sel(ReadReg1), .in_0(R0_out), .in_1(R1_out), .in_2(R2_out), .in_3(R3_out), .in_4(R4_out), .in_5(R5_out),
    .in_6(R6_out), .in_7(R7_out), .in_8(R8_out), .in_9(R9_out), .in_10(R10_out), .in_11(R11_out),
    .in_12(R12_out), .in_13(R13_out), .in_14(R14_out), .in_15(R15_out), .in_16(R16_out), .in_17(R17_out),
    .in_18(R18_out), .in_19(R19_out), .in_20(R20_out), .in_21(R21_out), .in_22(R22_out), .in_23(R23_out),
    .in_24(R24_out), .in_25(R25_out), .in_26(R26_out), .in_27(R27_out), .in_28(R28_out), .in_29(R29_out),
    .in_30(R30_out), .in_31(R31_out), .out(ReadData1));
  Multiplexer #(.Selector_Bits(5), .Bits(32)) multiplexer_2 (
    .sel(ReadReg2), .in_0(R0_out), .in_1(R1_out), .in_2(R2_out), .in_3(R3_out), .in_4(R4_out), .in_5(R5_out),
    .in_6(R6_out), .in_7(R7_out), .in_8(R8_out), .in_9(R9_out), .in_10(R10_out), .in_11(R11_out),
    .in_12(R12_out), .in_13(R13_out), .in_14(R14_out), .in_15(R15_out), .in_16(R16_out), .in_17(R17_out),
    .in_18(R18_out), .in_19(R19_out), .in_20(R20_out), .in_21(R21_out), .in_22(R22_out), .in_23(R23_out),
    .in_24(R24_out), .in_25(R25_out), .in_26(R26_out), .in_27(R27_out), .in_28(R28_out), .in_29(R29_out),
    .in_30(R30_out), .in_31(R31_out), .out(ReadData2));
endmodule

/* Test case Register File Test:
WriteReg WriteData RegWrite Clock ReadReg1 ReadReg2 ReadData1 ReadData2

# $1 = 25
1 25 1 C 1 0 25 0

# $2 = 30
2 30 1 C 0 2 0 30

# $(N+1) = (N+1)
loop(N, 30)
	(N+1) (N+1) 1 C (N+1) (N) (N+1) (N)
end loop

# $(N+1) = N-60
loop(N, 30)
	(N+1) (N-60) 1 C (N+1) (N+1) (N-60) (N-60)
end loop

# Try writing to $0. This should not write anything
0 25 1 C 0 0 0 0

# try writing when RegWrite = 0
# (the registers should still have their old values)
loop(N, 30)
	(N+1) (N+80) 0 C (N+1) (N+1) (N-60) (N-60)
end loop
*/
