// Digital circuit cpu.dig as structural Verilog
module cpu (
  input  clk,
  output [31:0] ReadData1,
  output [31:0] ReadData2
);

  wire [31:0] add_1_s, PC_q;

  Register #(.Bits(32), .isProgramCounter("true")) PC (.D(add_1_s), .C(clk), .en(1'b1), .Q(PC_q));
  Add #(.Bits(32)) add_1 (.a(32'h4), .b(PC_q), .c_i(1'b0), .s(add_1_s));  // open: c_o
  ROM #(.AddrBits(10), .isProgramMemory("true"), .Bits(32)) Instruction_Memory (.A(PC_q[11:2]), .sel(1'b1));  // open: D

  // Other names for the same wires on the sheet: clock = clk

  // Notes on the sheet:
  //   contents of Instruction_Memory (hex, n*v repeats v):
  //   20040005,2008000f,882020,843820,884825,e95025
endmodule

/* Test case cpu:
clk ReadData1 ReadData2
0 0 0		# addi $4 $0 -20
C (-20) 0 	# addi $5 $4 0x7FFF
C 32747 0 	# addi $6 $5 0x7018
C 61443 0 	# addi $7 $6 0x5311
C 0 0 		# ori $10 $0 10
C 10 0 		# ori $11 $10 0xFF55
C 65375 0 	# ori $12 $11 39
C 61443 0 	# andi $14 $6 0xE123
C 57347 0 	# andi $15 $14 0xFF1C
C 57344 0 	# andi $17 $15 0x541
C (-20) 0 	# slti $18 $4 311
C 1 0 		# slti $19 $18 2
C 1 0 		# slti $20 $19 0
C 0 0 		# slti $21 $20 -3	
C 0 0 		# slti $22 $21 5 
C 1 0 		# addi $0 $22 0 
C (-20) 0 	# slti $23 $4 -20	
C 0 0 		# addi $0 $23 0
C 65375 0 	# slti $24 $11 -90 
C 0 0 		# addi $0 $24 0
C (-20) 0 	# slti $25 $4 0 
C 1 0 		# addi $0 $25 0 
C 65375 0 	# slti $26 $11 6000
C 0 0 		# addi $0 $26 0 
C (-20) 0 	# slti $27 $4 -1 
C 1 0 		# addi $0 $27 0	
*/
